// Logisim project LDP5.circ as structural Verilog: 2 circuits, main circuit LDP5_1
module LDP5_1 (
  input  [31:0] A,
  input  [31:0] B,
  input  F2,
  input  [1:0] F1,
  output [31:0] Y
);

  wire adder_1_cout;
  wire [31:0] adder_1_out, and_1_out, bit_extender_1_out, multiplexer_2_out, not_1_out, or_1_out;

  Adder #(.width(32)) adder_1 (.a(A), .b(multiplexer_2_out), .out(adder_1_out), .cin(F2), .cout(adder_1_cout));
  Bit_Extender #(.in_width(32), .out_width(32)) bit_extender_1 (.in(adder_1_out), .out(bit_extender_1_out));
  Multiplexer #(.select(2), .width(32), .enable("false")) multiplexer_1 (
    .in0(and_1_out), .in1(or_1_out), .in2(adder_1_out), .in3(bit_extender_1_out), .out(Y), .sel(F1));
  assign not_1_out = ~B;  // NOT_Gate not_1, 32 bits wide
  Multiplexer #(.width(32), .enable("false")) multiplexer_2 (
    .in0(B), .in1(not_1_out), .out(multiplexer_2_out), .sel(F2));
  assign and_1_out = multiplexer_2_out & A;  // AND_Gate and_1, 32 bits wide
  assign or_1_out = multiplexer_2_out | A;  // OR_Gate or_1, 32 bits wide

  // Notes on the sheet:
  //   Cout
endmodule

module LDP5_2 (
  input  in_1,
  input  [4:0] A1,
  input  [4:0] A2,
  input  [4:0] A3,
  input  [31:0] WD3,
  output [31:0] RD1,
  output [31:0] RD2
);

  wire and_1_out, and_2_out, and_3_out, and_4_out, and_5_out, and_6_out, and_7_out, and_8_out, CLK_out,
       decoder_1_out0, decoder_1_out1, decoder_1_out2, decoder_1_out3, decoder_1_out4, decoder_1_out5,
       decoder_1_out6, decoder_1_out7;
  wire [31:0] register_1_q, register_2_q, register_3_q, register_4_q, register_5_q, register_6_q,
       register_7_q, register_8_q;

  Decoder #(.select(3), .enable("false")) decoder_1 (
    .out0(decoder_1_out0), .out1(decoder_1_out1), .out2(decoder_1_out2), .out3(decoder_1_out3),
    .out4(decoder_1_out4), .out5(decoder_1_out5), .out6(decoder_1_out6), .out7(decoder_1_out7), .sel(A3[2:0]));
  and and_1 (and_1_out, in_1, decoder_1_out0);
  and and_2 (and_2_out, decoder_1_out1, in_1);
  and and_3 (and_3_out, decoder_1_out2, in_1);
  and and_4 (and_4_out, decoder_1_out3, in_1);
  and and_5 (and_5_out, decoder_1_out4, in_1);
  and and_6 (and_6_out, decoder_1_out5, in_1);
  and and_7 (and_7_out, decoder_1_out6, in_1);
  and and_8 (and_8_out, decoder_1_out7, in_1);
  Register #(.width(32)) register_1 (.D(WD3), .en(and_1_out), .Q(register_1_q), .clk(CLK_out), .clr(1'b1));
  Register #(.width(32)) register_2 (.D(WD3), .en(and_2_out), .Q(register_2_q), .clk(CLK_out));  // open: clr
  Register #(.width(32)) register_3 (.D(WD3), .en(and_3_out), .Q(register_3_q), .clk(CLK_out));  // open: clr
  Register #(.width(32)) register_4 (.D(WD3), .en(and_4_out), .Q(register_4_q), .clk(CLK_out));  // open: clr
  Register #(.width(32)) register_5 (.D(WD3), .en(and_5_out), .Q(register_5_q), .clk(CLK_out));  // open: clr
  Register #(.width(32)) register_6 (.D(WD3), .en(and_6_out), .Q(register_6_q), .clk(CLK_out));  // open: clr
  Register #(.width(32)) register_7 (.D(WD3), .en(and_7_out), .Q(register_7_q), .clk(CLK_out));  // open: clr
  Register #(.width(32)) register_8 (.D(WD3), .en(and_8_out), .Q(register_8_q), .clk(CLK_out));  // open: clr
  Clock CLK (.out(CLK_out));
  Multiplexer #(.select(3), .width(32), .enable("false")) multiplexer_1 (
    .in0(register_1_q), .in1(register_2_q), .in2(register_3_q), .in3(register_4_q), .in4(register_5_q),
    .in5(register_6_q), .in6(register_7_q), .in7(register_8_q), .out(RD1), .sel(A1[2:0]));
  Multiplexer #(.select(3), .width(32), .enable("false")) multiplexer_2 (
    .in0(register_1_q), .in1(register_2_q), .in2(register_3_q), .in3(register_4_q), .in4(register_5_q),
    .in5(register_6_q), .in6(register_7_q), .in7(register_8_q), .out(RD2), .sel(A2[2:0]));

  // Notes on the sheet:
  //   REGISTER FILE
endmodule
