// Logisim project LDP8.circ as structural Verilog: 5 circuits, main circuit ALU
module ALU (
  input  [31:0] A,
  input  [31:0] B,
  input  [2:0] in_3,
  output [31:0] Y,
  output Z
);

  wire adder_1_cout;
  wire [31:0] adder_1_out, and_1_out, bit_extender_1_out, multiplexer_2_out, not_1_out, or_1_out;

  Adder #(.width(32)) adder_1 (.a(A), .b(multiplexer_2_out), .out(adder_1_out), .cin(in_3[2]), .cout(adder_1_cout));
  assign bit_extender_1_out = {{31{1'b0}}, adder_1_out[31]};  // Bit_Extender bit_extender_1
  Multiplexer #(.select(2), .width(32), .enable("false")) multiplexer_1 (
    .in0(and_1_out), .in1(or_1_out), .in2(adder_1_out), .in3(bit_extender_1_out), .out(Y), .sel(in_3[1:0]));
  assign not_1_out = ~B;  // NOT_Gate not_1, 32 bits wide
  Multiplexer #(.width(32), .enable("false")) multiplexer_2 (
    .in0(B), .in1(not_1_out), .out(multiplexer_2_out), .sel(in_3[2]));
  assign and_1_out = multiplexer_2_out & A;  // AND_Gate and_1, 32 bits wide
  assign or_1_out = multiplexer_2_out | A;  // OR_Gate or_1, 32 bits wide
  not not_2 (Z, Y[0]);
endmodule

module Register (
  input  in_1,
  input  WE3,
  input  [4:0] A1,
  input  [4:0] A2,
  input  [4:0] A3,
  input  [31:0] WD3,
  output [31:0] RD1,
  output [31:0] RD2
);

  wire and_1_out, and_2_out, and_3_out, and_4_out, and_5_out, and_6_out, and_7_out, and_8_out,
       decoder_1_out0, decoder_1_out1, decoder_1_out2, decoder_1_out3, decoder_1_out4, decoder_1_out5,
       decoder_1_out6, decoder_1_out7;
  wire [31:0] register_1_q, register_2_q, register_3_q, register_4_q, register_5_q, register_6_q,
       register_7_q, register_8_q;

  Decoder #(.select(3), .enable("false")) decoder_1 (
    .out0(decoder_1_out0), .out1(decoder_1_out1), .out2(decoder_1_out2), .out3(decoder_1_out3),
    .out4(decoder_1_out4), .out5(decoder_1_out5), .out6(decoder_1_out6), .out7(decoder_1_out7), .sel(A3[2:0]));
  and and_1 (and_1_out, WE3, decoder_1_out0);
  and and_2 (and_2_out, decoder_1_out1, WE3);
  and and_3 (and_3_out, decoder_1_out2, WE3);
  and and_4 (and_4_out, decoder_1_out3, WE3);
  and and_5 (and_5_out, decoder_1_out4, WE3);
  and and_6 (and_6_out, decoder_1_out5, WE3);
  and and_7 (and_7_out, decoder_1_out6, WE3);
  and and_8 (and_8_out, decoder_1_out7, WE3);
  Register_part #(.width(32)) register_1 (.en(and_1_out), .Q(register_1_q), .clk(in_1));  // open: D, clr
  Register_part #(.width(32)) register_2 (.D(WD3), .en(and_2_out), .Q(register_2_q), .clk(in_1));  // open: clr
  Register_part #(.width(32)) register_3 (.D(WD3), .en(and_3_out), .Q(register_3_q), .clk(in_1));  // open: clr
  Register_part #(.width(32)) register_4 (.D(WD3), .en(and_4_out), .Q(register_4_q), .clk(in_1));  // open: clr
  Register_part #(.width(32)) register_5 (.D(WD3), .en(and_5_out), .Q(register_5_q), .clk(in_1));  // open: clr
  Register_part #(.width(32)) register_6 (.D(WD3), .en(and_6_out), .Q(register_6_q), .clk(in_1));  // open: clr
  Register_part #(.width(32)) register_7 (.D(WD3), .en(and_7_out), .Q(register_7_q), .clk(in_1));  // open: clr
  Register_part #(.width(32)) register_8 (.D(WD3), .en(and_8_out), .Q(register_8_q), .clk(in_1));  // open: clr
  Multiplexer #(.select(3), .width(32), .enable("false")) multiplexer_1 (
    .in0(register_1_q), .in1(register_2_q), .in2(register_3_q), .in3(register_4_q), .in4(register_5_q),
    .in5(register_6_q), .in6(register_7_q), .in7(register_8_q), .out(RD1), .sel(A1[2:0]));
  Multiplexer #(.select(3), .width(32), .enable("false")) multiplexer_2 (
    .in0(register_1_q), .in1(register_2_q), .in2(register_3_q), .in3(register_4_q), .in4(register_5_q),
    .in5(register_6_q), .in6(register_7_q), .in7(register_8_q), .out(RD2), .sel(A2[2:0]));
endmodule

module All_Instructions (
);

  wire alu_1_z, and_1_out, clk_out, opcode_decoder_1_aluop1, opcode_decoder_1_aluop2,
       opcode_decoder_1_alusrc, opcode_decoder_1_branch, opcode_decoder_1_mem2_reg,
       opcode_decoder_1_mem2write, opcode_decoder_1_regdst, opcode_decoder_1_regwrite;
  wire [1:0] PC_q, ram_1_data_2;
  wire [2:0] alu_decoder_1_op0;
  wire [4:0] multiplexer_3_out;
  wire [5:0] ram_1_data_3;
  wire [13:0] PC_q_2;
  wire [15:0] PC_q_3;
  wire [25:0] ram_1_data;
  wire [31:0] adder_1_out, adder_2_out, alu_1_y, bit_extender_1_out, multiplexer_1_out, multiplexer_2_out,
       multiplexer_4_out, ram_2_data, register_1_rd1, register_1_rd2, shifter_1_out;

  Multiplexer #(.width(32), .enable("false")) multiplexer_1 (
    .in0(adder_1_out), .in1(adder_2_out), .out(multiplexer_1_out), .sel(and_1_out));
  Register_part #(.width(32), .trigger("falling")) PC (
    .D(multiplexer_1_out), .Q({PC_q_3, PC_q_2, PC_q}), .clk(clk_out));  // open: en, clr
  Adder #(.width(32)) adder_1 (.a({PC_q_3, PC_q_2, PC_q}), .b(32'h4), .out(adder_1_out));  // open: cin, cout
  ALU_Decoder alu_decoder_1 (
    .f3(ram_1_data[3]), .f2(ram_1_data[2]), .f1(ram_1_data[1]), .f0(ram_1_data[0]),
    .ALUOP2(opcode_decoder_1_aluop1), .ALUOP1(opcode_decoder_1_aluop2), .op1(alu_decoder_1_op0[1]),
    .op2(alu_decoder_1_op0[2]), .op0(alu_decoder_1_op0[0]));
  Opcode_Decoder opcode_decoder_1 (
    .op5(ram_1_data_3[5]), .op4(ram_1_data_3[4]), .op3(ram_1_data_3[3]), .op2(ram_1_data_3[2]),
    .op1(ram_1_data_3[1]), .op0(ram_1_data_3[0]), .REGDST(opcode_decoder_1_regdst),
    .mem2write(opcode_decoder_1_mem2write), .mem2_reg(opcode_decoder_1_mem2_reg),
    .branch(opcode_decoder_1_branch), .regwrite(opcode_decoder_1_regwrite), .ALUsrc(opcode_decoder_1_alusrc),
    .ALUOP1(opcode_decoder_1_aluop1), .ALUOP2(opcode_decoder_1_aluop2));
  RAM #(.addrWidth(14), .dataWidth(32)) ram_1 (
    .addr(PC_q_2), .data({ram_1_data_3, ram_1_data[25:6], ram_1_data_2, ram_1_data[3:0]}));  // open: sel, clk, ld, clr
  Clock clk (.out(clk_out));
  Register register_1 (
    .A1(ram_1_data[25:21]), .A2(ram_1_data[20:16]), .A3(multiplexer_3_out), .WD3(multiplexer_4_out),
    .RD1(register_1_rd1), .RD2(register_1_rd2), .WE3(opcode_decoder_1_regwrite), .in_1(clk_out));
  assign bit_extender_1_out = {{16{ram_1_data[15]}}, {ram_1_data[15:6], ram_1_data_2, ram_1_data[3:0]}};  // Bit_Extender bit_extender_1
  Multiplexer #(.width(32), .enable("false")) multiplexer_2 (
    .in0(register_1_rd2), .in1(bit_extender_1_out), .out(multiplexer_2_out), .sel(opcode_decoder_1_alusrc));
  ALU alu_1 (.A(register_1_rd1), .B(multiplexer_2_out), .Y(alu_1_y), .in_3(alu_decoder_1_op0), .Z(alu_1_z));
  Multiplexer #(.width(5), .enable("false")) multiplexer_3 (
    .in0(ram_1_data[20:16]), .in1(ram_1_data[15:11]), .out(multiplexer_3_out), .sel(opcode_decoder_1_regdst));
  Shifter #(.width(32)) shifter_1 (.in(bit_extender_1_out), .\dist (5'b00010), .out(shifter_1_out));
  and and_1 (and_1_out, opcode_decoder_1_branch, alu_1_z);
  Adder #(.width(32)) adder_2 (.a(shifter_1_out), .b(adder_1_out), .out(adder_2_out));  // open: cin, cout
  RAM #(.addrWidth(14), .dataWidth(32), .bus("separate")) ram_2 (
    .addr(alu_1_y[15:2]), .din(register_1_rd2), .data(ram_2_data), .str(opcode_decoder_1_mem2write),
    .clk(clk_out));  // open: sel, ld, clr
  Multiplexer #(.width(32), .enable("false")) multiplexer_4 (
    .in0(alu_1_y), .in1(ram_2_data), .out(multiplexer_4_out), .sel(opcode_decoder_1_mem2_reg));
endmodule

module Opcode_Decoder (
  input  op5,
  input  op4,
  input  op3,
  input  op2,
  input  op1,
  input  op0,
  output REGDST,
  output mem2write,
  output mem2_reg,
  output branch,
  output regwrite,
  output ALUsrc,
  output ALUOP1,
  output ALUOP2
);

  wire addi_out;

  and r_type (ALUOP1, ~op5, ~op4, ~op3, ~op2, ~op1, ~op0);  // AND_Gate
  and lw (mem2_reg, op5, ~op4, ~op3, ~op2, op1, op0);  // AND_Gate
  and sw (mem2write, op5, ~op4, op3, ~op2, op1, op0);  // AND_Gate
  and beq (ALUOP2, ~op5, ~op4, ~op3, op2, ~op1, ~op0);  // AND_Gate
  and addi (addi_out, ~op5, ~op4, op3, ~op2, ~op1, ~op0);  // AND_Gate
  or or_1 (regwrite, ALUOP1, mem2_reg, addi_out);
  or or_2 (ALUsrc, mem2_reg, mem2write, addi_out);

  assign branch = ALUOP2;
  assign REGDST = ALUOP1;
endmodule

module ALU_Decoder (
  input  ALUOP2,
  input  ALUOP1,
  input  f3,
  input  f2,
  input  f1,
  input  f0,
  output op1,
  output op2,
  output op0
);

  wire and_2_out, or_1_out;

  or or_1 (or_1_out, f3, f0);
  and and_1 (op0, ALUOP2, or_1_out);
  or or_2 (op1, ~ALUOP2, ~f2);  // OR_Gate
  and and_2 (and_2_out, ALUOP2, f1);
  or or_3 (op2, ALUOP1, and_2_out);
endmodule
